// Logisim project cpu.circ as structural Verilog: 14 circuits, main circuit Controller
module cpu (
);

  wire CLK, npc_1_out_12, RST;
  wire [1:0] ex_mem_1_out_9;
  wire [2:0] controller_1_out_12;
  wire [3:0] ex_mem_1_out_9_2;
  wire [4:0] controller_1_out_11, decoder_1_out_2, decoder_1_out_4, decoder_1_out_6, decoder_1_out_8,
       ex_mem_1_out_8, id_ex_1_out_11, mem_wb_1_out_7, multiplexer_2_out, multiplexer_3_out,
       registerfile_1_p6;
  wire [5:0] controller_1_out_9, controller_1_out_10, decoder_1_out_3, decoder_1_out_7, id_ex_1_out_12,
       id_ex_1_out_13;
  wire [9:0] divider_1_out_2;
  wire [15:0] decoder_1_out_9, \总周期数 , \无条件分支指令数 , \有条件分支成功跳转 , \有条件分支指令数 ;
  wire [23:0] divider1_1_out_2;
  wire [25:0] decoder_1_out_5;
  wire [31:0] alu_1_result, ex_mem_1_out_10, ex_mem_1_out_11, extender_1_out_3, extender_1_out_4,
       id_ex_1_out_15, id_ex_1_out_16, id_ex_1_out_17, if_id_1_out_6, if_id_1_out_7, mem_wb_1_out_8,
       mem_wb_1_out_9, mips_ram_1_p8, multiplexer_1_out, multiplexer_5_out, multiplexer_6_out, npc_1_out_11,
       npc_1_out_13, PC_q, registerfile_1_p7, registerfile_1_p8, rom_1_data, SyscallOut;

  Clock clock_1 (.out(CLK));
  Button \u_总复位  (.out(RST));
  SumPeriod sumperiod_1 (.in_1(npc_1_out_12), .in_2(CLK), .out_4(\总周期数 ), .in_3(RST));
  Register #(.width(32)) PC (.D(npc_1_out_11), .en(npc_1_out_12), .Q(PC_q), .clk(CLK), .clr(RST));
  Hex_Digit_Display hex_digit_display_1 (.value(SyscallOut[27:24]));  // open: dp
  Hex_Digit_Display hex_digit_display_2 (.value(SyscallOut[31:28]));  // open: dp
  Divider divider_1 (.in_1(PC_q), .out_2(divider_1_out_2));
  NPC npc_1 (
    .in_2(PC_q), .out_11(npc_1_out_11), .in_9(decoder_1_out_5), .in_1(decoder_1_out_9),
    .out_13(npc_1_out_13), .in_8(RST), .in_7(CLK), .out_14(\有条件分支成功跳转 ), .out_12(npc_1_out_12));  // open: in_5, in_6, in_10, in_4, in_3
  Hex_Digit_Display hex_digit_display_3 (.value(SyscallOut[19:16]));  // open: dp
  Hex_Digit_Display hex_digit_display_4 (.value(SyscallOut[23:20]));  // open: dp
  Hex_Digit_Display hex_digit_display_5 (.value(SyscallOut[11:8]));  // open: dp
  Hex_Digit_Display hex_digit_display_6 (.value(SyscallOut[15:12]));  // open: dp
  Hex_Digit_Display hex_digit_display_7 (.value(SyscallOut[7:4]));  // open: dp
  Hex_Digit_Display hex_digit_display_8 (.value(SyscallOut[3:0]));  // open: dp
  ROM #(.addrWidth(10), .dataWidth(32)) rom_1 (.addr(divider_1_out_2), .data(rom_1_data));  // open: sel
  IF_ID if_id_1 (
    .in_1(npc_1_out_13), .in_2(rom_1_data), .out_6(if_id_1_out_6), .out_7(if_id_1_out_7));  // open: 传输状态In, CLK, 传输状态Out, 同步清零
  // Probe on \总周期数 
  // Probe on \无条件分支指令数 
  // Probe on \有条件分支指令数 
  // Probe on \有条件分支成功跳转 
  Controller controller_1 (
    .in_1(decoder_1_out_3), .in_2(decoder_1_out_7), .in_3(CLK), .in_4(RST), .out_6(\有条件分支指令数 ),
    .out_7(\无条件分支指令数 ), .out_9(controller_1_out_9), .out_12(controller_1_out_12),
    .out_10(controller_1_out_10), .out_11(controller_1_out_11));  // open: out_5, out_8
  Decoder decoder_1 (
    .out_2(decoder_1_out_2), .out_3(decoder_1_out_3), .out_4(decoder_1_out_4), .out_5(decoder_1_out_5),
    .in_1(if_id_1_out_7), .out_6(decoder_1_out_6), .out_7(decoder_1_out_7), .out_8(decoder_1_out_8),
    .out_9(decoder_1_out_9));
  Multiplexer #(.select(2), .width(32), .disabled(0), .enable("false")) multiplexer_1 (
    .in0(mem_wb_1_out_9), .in1(if_id_1_out_6), .in3(mem_wb_1_out_8), .out(multiplexer_1_out),
    .sel(mem_wb_1_out_7[3:2]));  // open: in2
  Multiplexer #(.select(2), .width(5), .disabled(0), .enable("false")) multiplexer_2 (
    .in0(decoder_1_out_8), .in1(decoder_1_out_6), .in2({5{1'b1}}), .out(multiplexer_2_out),
    .sel(mem_wb_1_out_7[1:0]));  // open: in3
  Multiplexer #(.width(5), .disabled(0), .enable("false")) multiplexer_3 (
    .in0(decoder_1_out_4), .in1(5'b00010), .out(multiplexer_3_out), .sel(controller_1_out_12[1]));
  // RegisterFile registerfile_1: pin names not known; wires that end beside it: multiplexer_1_out, CLK, mem_wb_1_out_7[4], multiplexer_2_out, multiplexer_3_out, registerfile_1_p6, registerfile_1_p7, registerfile_1_p8
  Syscall1 syscall1_1 (
    .in_1(controller_1_out_12[0]), .out_5(SyscallOut), .in_2(CLK), .in_3(RST), .in_4(registerfile_1_p8));
  Multiplexer #(.width(5), .disabled(0), .enable("false")) multiplexer_4 (
    .in0(decoder_1_out_6), .in1(5'b00100), .out(registerfile_1_p6), .sel(controller_1_out_12[2]));
  Extender extender_1 (
    .in_1(decoder_1_out_2), .out_3(extender_1_out_3), .out_4(extender_1_out_4), .in_2(decoder_1_out_9));
  ID_EX id_ex_1 (
    .in_1(controller_1_out_11), .in_2(controller_1_out_10), .in_3(controller_1_out_9),
    .in_4(registerfile_1_p7), .in_5(registerfile_1_p8), .in_6(extender_1_out_3), .in_7(extender_1_out_4),
    .out_11(id_ex_1_out_11), .out_12(id_ex_1_out_12), .out_13(id_ex_1_out_13), .out_14(registerfile_1_p7),
    .out_15(id_ex_1_out_15), .out_16(id_ex_1_out_16), .out_17(id_ex_1_out_17));  // open: 传输状态In, CLK, 传输状态Out, 同步清零
  Multiplexer #(.width(32), .disabled(0), .enable("false")) multiplexer_5 (
    .in0(registerfile_1_p7), .in1(id_ex_1_out_16), .out(multiplexer_5_out), .sel(id_ex_1_out_13[0]));
  ALU alu_1 (.AluOP(id_ex_1_out_13[5:2]), .X(multiplexer_5_out), .Result(alu_1_result), .Y(multiplexer_6_out));
  Multiplexer #(.width(32), .disabled(0), .enable("false")) multiplexer_6 (
    .in0(id_ex_1_out_15), .in1(id_ex_1_out_17), .out(multiplexer_6_out), .sel(id_ex_1_out_13[1]));
  EX_MEM ex_mem_1 (
    .in_1(id_ex_1_out_11), .in_2(id_ex_1_out_12), .in_3(alu_1_result), .in_4(id_ex_1_out_15),
    .out_8(ex_mem_1_out_8), .out_9({ex_mem_1_out_9_2, ex_mem_1_out_9}), .out_10(ex_mem_1_out_10),
    .out_11(ex_mem_1_out_11));  // open: 传输状态In, CLK, 传输状态Out, 同步清零
  Divider1 divider1_1 (.in_1(ex_mem_1_out_10), .out_2(divider1_1_out_2));
  // MIPS_RAM mips_ram_1: pin names not known; wires that end beside it: divider1_1_out_2, ex_mem_1_out_11, ex_mem_1_out_9[1], ex_mem_1_out_9_2, CLK, ex_mem_1_out_9[0], RST, mips_ram_1_p8
  MEM_WB mem_wb_1 (
    .in_1(ex_mem_1_out_8), .out_7(mem_wb_1_out_7), .in_3(ex_mem_1_out_10), .out_9(mem_wb_1_out_9),
    .in_2(mips_ram_1_p8), .out_8(mem_wb_1_out_8));  // open: 传输状态In, CLK, 传输状态Out, 同步清零

  // Notes on the sheet:
  //   数码管输出应该用寄存器锁存，否则显示数据只能一闪而过
  //   可以通过项目增加Logisim库的方式将前几次实验完成的电路作为子电路引入到本电路中使用
  //   数码管输出
  //   contents of rom_1 (hex, n*v repeats v):
  //   20110001 8000c05 20110001 20120002 20130003 8000c09 20110001 20120002 20130003 8000c0d 20110001
  //   20120002 20130003 8000c11 20110001 20120002 20130003 c000cb8 20100001 20110001 118fc0 112020
  //   20020022 c 118882 12200001 8000c15 112020 20020022 c 20110001 118880 112020 20020022 c 12200001
  //   8000c1f 20110001 118fc0 112020 20020022 c 1188c3 112020 20020022 c 118903 112020 20020022 c 118903
  //   112020 20020022 c 118903 112020 20020022 c 118903 112020 20020022 c 118903 112020 20020022 c 118903
  //   112020 20020022 c 118903 112020 20020022 c 20100001 109fc0 139fc3 8021 2012000c 24160003 26100001
  //   3210000f 20080008 20090001 139900 2709825 132020 20020022 c 1094022 1500fff9 22100001 2018000f
  //   2188024 108700 20080008 20090001 139902 2709825 132021 20020022 c 1094022 1500fff9 108702 2c9b022
  //   12c00001 8000c50 4020 1084027 84400 3508ffff 82021 20020022 c 2010ffff 20110000 ae300000 22100001
  //   22310004 ae300000 22100001 22310004 ae300000 22100001 22310004 ae300000 22100001 22310004 ae300000
  //   22100001 22310004 ae300000 22100001 22310004 ae300000 22100001 22310004 ae300000 22100001 22310004
  //   ae300000 22100001 22310004 ae300000 22100001 22310004 ae300000 22100001 22310004 ae300000 22100001
  //   22310004 ae300000 22100001 22310004 ae300000 22100001 22310004 ae300000 22100001 22310004 ae300000
  //   22100001 22310004 22100001 8020 2011003c 8e130000 8e340000 274402a 11000002 ae330000 ae140000
  //   2231fffc 1611fff8 102020 20020022 c 22100004 2011003c 1611fff2 2002000a c 20100000 22100001 102020
  //   20020022 c 22100002 102020 20020022 c 22100003 102020 20020022 c 22100004 102020 20020022 c 22100005
  //   102020 20020022 c 22100006 102020 20020022 c 22100007 102020 20020022 c 22100008 102020 20020022
  //   20020022 c 3e00008
  //   总复位信号应将除ROM以外所有存储组件全部清零
  //   alu
  //   pc4
  //   load
endmodule

module Controller (
  input  [5:0] in_1,
  input  [5:0] in_2,
  input  in_3,
  input  in_4,
  output [2:0] out_5,
  output [15:0] out_6,
  output [15:0] out_7,
  output out_8,
  output [5:0] out_9,
  output [5:0] out_10,
  output [4:0] out_11,
  output [2:0] out_12
);

  wire add, addi, addiu, adds, addu, \and , andi, ands, beq, bltz, bne, cmps, comparator_1_eq,
       comparator_16_eq, comparator_17_eq, comparator_18_eq, comparator_19_eq, comparator_20_eq,
       comparator_21_eq, comparator_22_eq, comparator_23_eq, comparator_24_eq, comparator_25_eq,
       comparator_26_eq, comparator_27_eq, comparator_28_eq, comparator_29_eq, j, jal, jr, js, \nor , \or ,
       or_6_out, or_9_out, or_10_out, or_11_out, ori, ors, rlshifters, sb, sll, slt, slti, sltu, sra, srl,
       srlv, sub, sw, xori;

  Comparator #(.width(6)) comparator_1 (.a(in_1), .b({6{1'b0}}), .eq(comparator_1_eq));  // open: gt, lt
  Comparator #(.width(6)) comparator_2 (.a(in_1), .b(6'b001000), .eq(addi));  // open: gt, lt
  Comparator #(.width(6)) comparator_3 (.a(in_1), .b(6'b001001), .eq(addiu));  // open: gt, lt
  Comparator #(.width(6)) comparator_4 (.a(in_1), .b(6'b001100), .eq(andi));  // open: gt, lt
  Comparator #(.width(6)) comparator_5 (.a(in_1), .b(6'b001101), .eq(ori));  // open: gt, lt
  Comparator #(.width(6)) comparator_6 (.a(in_1), .b(6'b001110), .eq(xori));  // open: gt, lt
  Comparator #(.width(6)) comparator_7 (.a(in_1), .b(6'b001010), .eq(slti));  // open: gt, lt
  Comparator #(.width(6)) comparator_8 (.a(in_1), .b(6'b100011), .eq(out_10[0]));  // open: gt, lt
  Comparator #(.width(6)) comparator_9 (.a(in_1), .b(6'b101011), .eq(sw));  // open: gt, lt
  Comparator #(.width(6)) comparator_10 (.a(in_1), .b(6'b101000), .eq(sb));  // open: gt, lt
  Comparator #(.width(6)) comparator_11 (.a(in_1), .b(6'b000100), .eq(beq));  // open: gt, lt
  Comparator #(.width(6)) comparator_12 (.a(in_1), .b(6'b000101), .eq(bne));  // open: gt, lt
  Comparator #(.width(6)) comparator_13 (.a(in_1), .b(6'b000001), .eq(bltz));  // open: gt, lt
  Comparator #(.width(6)) comparator_14 (.a(in_1), .b(6'b000010), .eq(j));  // open: gt, lt
  Comparator #(.width(6)) comparator_15 (.a(in_1), .b(6'b000011), .eq(jal));  // open: gt, lt
  Comparator #(.width(6)) comparator_16 (.a(in_2), .b(6'b100000), .eq(comparator_16_eq));  // open: gt, lt
  Comparator #(.width(6)) comparator_17 (.a(in_2), .b(6'b100001), .eq(comparator_17_eq));  // open: gt, lt
  Comparator #(.width(6)) comparator_18 (.a(in_2), .b(6'b100100), .eq(comparator_18_eq));  // open: gt, lt
  Comparator #(.width(6)) comparator_19 (.a(in_2), .b(6'b100010), .eq(comparator_19_eq));  // open: gt, lt
  Comparator #(.width(6)) comparator_20 (.a(in_2), .b(6'b100101), .eq(comparator_20_eq));  // open: gt, lt
  Comparator #(.width(6)) comparator_21 (.a(in_2), .b(6'b100111), .eq(comparator_21_eq));  // open: gt, lt
  Comparator #(.width(6)) comparator_22 (.a(in_2), .b(6'b000110), .eq(comparator_22_eq));  // open: gt, lt
  Comparator #(.width(6)) comparator_23 (.a(in_2), .b(6'b101010), .eq(comparator_23_eq));  // open: gt, lt
  Comparator #(.width(6)) comparator_24 (.a(in_2), .b(6'b101011), .eq(comparator_24_eq));  // open: gt, lt
  Comparator #(.width(6)) comparator_25 (.a(in_2), .b({6{1'b0}}), .eq(comparator_25_eq));  // open: gt, lt
  Comparator #(.width(6)) comparator_26 (.a(in_2), .b(6'b000011), .eq(comparator_26_eq));  // open: gt, lt
  Comparator #(.width(6)) comparator_27 (.a(in_2), .b(6'b000010), .eq(comparator_27_eq));  // open: gt, lt
  Comparator #(.width(6)) comparator_28 (.a(in_2), .b(6'b001000), .eq(comparator_28_eq));  // open: gt, lt
  Comparator #(.width(6)) comparator_29 (.a(in_2), .b(6'b001100), .eq(comparator_29_eq));  // open: gt, lt
  and and_1 (add, comparator_1_eq, comparator_16_eq);
  and and_2 (addu, comparator_1_eq, comparator_17_eq);
  and and_3 (\and , comparator_1_eq, comparator_18_eq);
  and and_4 (sub, comparator_1_eq, comparator_19_eq);
  and and_5 (\or , comparator_1_eq, comparator_20_eq);
  and and_6 (\nor , comparator_1_eq, comparator_21_eq);
  and and_7 (srlv, comparator_1_eq, comparator_22_eq);
  and and_8 (slt, comparator_1_eq, comparator_23_eq);
  and and_9 (sltu, comparator_1_eq, comparator_24_eq);
  and and_10 (sll, comparator_1_eq, comparator_25_eq);
  and and_11 (sra, comparator_1_eq, comparator_26_eq);
  and and_12 (srl, comparator_1_eq, comparator_27_eq);
  and and_13 (jr, comparator_1_eq, comparator_28_eq);
  and and_14 (out_12[0], comparator_1_eq, comparator_29_eq);
  or or_1 (cmps, slti, bltz, slt);
  or or_2 (ors, \or , ori);
  or or_3 (ands, \and , andi);
  or or_4 (rlshifters, srlv, srl);
  or or_5 (out_9[0], sll, sra, srl);
  or or_6 (or_6_out, addi, addiu, andi, ori, xori, slti, out_10[0], sw, sb);
  or or_7 (adds, out_10[0], add, addi, sb, addu, addiu, sw);
  Priority_Encoder #(.select(4)) priority_encoder_1 (
    .in0(1'b1), .in1(sra), .in2(rlshifters), .in3(1'b0), .in4(1'b0), .in5(adds), .in6(sub), .in7(ands),
    .in8(ors), .in9(xori), .in10(\nor ), .in11(cmps), .in12(sltu), .in13(1'b0), .in14(1'b0), .in15(1'b0),
    .out(out_9[5:2]));  // open: gs, en_out, en_in
  Priority_Encoder #(.select(1)) priority_encoder_2 (
    .in0(1'b1), .in1(or_6_out), .out(out_9[1]));  // open: gs, en_out, en_in
  not not_1 (out_10[5], sb);
  or or_8 (out_10[1], sw, sb);
  Priority_Encoder #(.select(1)) priority_encoder_3 (
    .in0(1'b1), .in1(out_12[0]), .out(out_12[2]));  // open: gs, en_out, en_in
  or or_9 (or_9_out, addi, addiu, andi, ori, xori, slti, out_10[0]);
  Priority_Encoder #(.select(2)) priority_encoder_4 (
    .in0(1'b1), .in1(jal), .in2(out_10[0]), .in3(1'b0), .out(out_11[3:2]));  // open: gs, en_out, en_in
  nor nor_1 (out_11[4], sw, sb, beq, bne, bltz, j, jr, out_12[0]);
  Priority_Encoder #(.select(2)) priority_encoder_5 (
    .in0(1'b1), .in1(or_9_out), .in2(jal), .in3(1'b0), .out(out_11[1:0]));  // open: gs, en_out, en_in
  or or_10 (or_10_out, bltz, bne, beq);
  or or_11 (or_11_out, j, jal, jr);
  or or_12 (js, j, jal);
  Priority_Encoder priority_encoder_6 (
    .in0(1'b1), .in1(beq), .in2(bne), .in3(bltz), .in4(js), .in5(jr), .in6(1'b0), .in7(1'b0), .out(out_5));  // open: en_in, gs, en_out
  not not_2 (out_8, out_12[0]);
  Counter #(.width(16), .max('hffff)) counter_1 (
    .count(or_10_out), .Q(out_6), .clk(in_3), .clr(in_4));  // open: load, D, carry
  Counter #(.width(16), .max('hffff)) counter_2 (
    .count(or_11_out), .Q(out_7), .clk(in_3), .clr(in_4));  // open: load, D, carry

  assign out_10[4:2] = {{2{out_10[5]}}, 1'b1};
  assign out_12[1] = out_12[2];

  // Other names for the same wires on the sheet: CLK = in_3; CPC[2:0] = out_5; funct[5:0] = in_2; op[5:0] = in_1;
  //   CA = out_9[0]; CB = out_9[1]; ALUop[3:0] = out_9[5:2]; ld = out_10[0]; lw = out_10[0]; str = out_10[1];
  //   Sel[3:1] = {3{out_10[5]}}; Rw[1:0] = out_11[1:0]; Din[1:0] = out_11[3:2]; We = out_11[4]; SysC1 = out_12[0];
  //   syscall = out_12[0]; Ra = out_12[2]; Rb = out_12[2]; RST = in_4; SysC2 = out_8; 无条件[15:0] = out_7;
  //   有条件[15:0] = out_6
endmodule

module NPC (
  input  [15:0] in_1,
  input  [31:0] in_2,
  input  [31:0] in_3,
  input  in_4,
  input  [31:0] in_5,
  input  [2:0] in_6,
  input  in_7,
  input  in_8,
  input  [25:0] in_9,
  input  [31:0] in_10,
  output [31:0] out_11,
  output out_12,
  output [31:0] out_13,
  output [15:0] out_14
);

  wire and_2_out, and_3_out, and_4_out, comparator_1_eq, comparator_2_eq, comparator_3_lt, comparator_4_eq,
       comparator_5_eq, comparator_6_eq, not_1_out, or_3_out;
  wire [31:0] and_1_out, bit_extender_1_out, bit_extender_2_out, Cbeq, Cbltz, Cbne, PC4offset, PCLabel;

  Adder #(.width(32)) adder_1 (.a(in_2), .b(32'h4), .out(out_13));  // open: cin, cout
  Comparator #(.width(32)) comparator_1 (.a(in_5), .b(32'h22), .eq(comparator_1_eq));  // open: gt, lt
  assign bit_extender_1_out = {{14{in_1[15]}}, {in_1, 2'b00}};  // Bit_Extender bit_extender_1
  assign and_1_out = in_2 & 32'hf0000000;  // AND_Gate and_1, 32 bits wide
  assign bit_extender_2_out = {{4{1'b0}}, {in_9, 2'b00}};  // Bit_Extender bit_extender_2
  Adder #(.width(32)) adder_2 (.a(bit_extender_1_out), .b(in_3), .out(PC4offset));  // open: cin, cout
  assign PCLabel = and_1_out | bit_extender_2_out;  // OR_Gate or_1, 32 bits wide
  or or_2 (out_12, comparator_1_eq, in_4);
  Comparator #(.width(32)) comparator_2 (.a(in_5), .b(in_10), .eq(comparator_2_eq));  // open: gt, lt
  Comparator #(.width(32)) comparator_3 (.a(in_5), .b(in_10), .lt(comparator_3_lt));  // open: gt, eq
  Multiplexer #(.width(32), .disabled(0), .enable("false")) multiplexer_1 (
    .in0(in_3), .in1(PC4offset), .out(Cbeq), .sel(comparator_2_eq));
  Multiplexer #(.width(32), .disabled(0), .enable("false")) multiplexer_2 (
    .in0(PC4offset), .in1(in_3), .out(Cbne), .sel(comparator_2_eq));
  Comparator #(.width(3)) comparator_4 (.a(in_6), .b(3'b001), .eq(comparator_4_eq));  // open: gt, lt
  Comparator #(.width(3)) comparator_5 (.a(in_6), .b(3'b010), .eq(comparator_5_eq));  // open: gt, lt
  not not_1 (not_1_out, comparator_2_eq);
  Comparator #(.width(3)) comparator_6 (.a(in_6), .b(3'b011), .eq(comparator_6_eq));  // open: gt, lt
  Multiplexer #(.width(32), .disabled(0), .enable("false")) multiplexer_3 (
    .in0(in_3), .in1(PC4offset), .out(Cbltz), .sel(comparator_3_lt));
  and and_2 (and_2_out, comparator_4_eq, comparator_2_eq);
  and and_3 (and_3_out, comparator_5_eq, not_1_out);
  and and_4 (and_4_out, comparator_6_eq, comparator_3_lt);
  Counter #(.width(16), .max('hffff)) counter_1 (
    .count(or_3_out), .Q(out_14), .clk(in_7), .clr(in_8));  // open: load, D, carry
  or or_3 (or_3_out, and_2_out, and_3_out, and_4_out);
  Multiplexer #(.select(3), .width(32), .disabled(0), .enable("false")) multiplexer_4 (
    .in0(in_3), .in1(Cbeq), .in2(Cbne), .in3(Cbltz), .in4(PCLabel), .in5(in_5), .in6({32{1'b0}}),
    .in7({32{1'b0}}), .out(out_11), .sel(in_6));

  // Other names for the same wires on the sheet: IMM[15:0] = in_1; label[25:0] = in_9; CLK = in_7; CNPC[2:0] = in_6;
  //   en = out_12; Input[31:0] = in_2; oldPC4[31:0] = in_3; Output[31:0] = out_11; PC4[31:0] = out_13;
  //   RF1[31:0] = in_5; RF2[31:0] = in_10; RST = in_8; success[15:0] = out_14; syscall = in_4
endmodule

module Divider (
  input  [31:0] in_1,
  output [9:0] out_2
);


  assign out_2 = in_1[11:2];

  // Other names for the same wires on the sheet: Input[31:0] = in_1; Output[9:0] = in_1[11:2]
endmodule

module Divider1 (
  input  [31:0] in_1,
  output [23:0] out_2
);


  assign out_2 = in_1[25:2];

  // Other names for the same wires on the sheet: Input[31:0] = in_1; Output[23:0] = in_1[25:2]
endmodule

module Decoder (
  input  [31:0] in_1,
  output [4:0] out_2,
  output [5:0] out_3,
  output [4:0] out_4,
  output [25:0] out_5,
  output [4:0] out_6,
  output [5:0] out_7,
  output [4:0] out_8,
  output [15:0] out_9
);


  assign out_2 = in_1[10:6];
  assign out_3 = in_1[31:26];
  assign out_4 = in_1[25:21];
  assign out_5 = in_1[25:0];
  assign out_6 = in_1[20:16];
  assign out_7 = in_1[5:0];
  assign out_8 = in_1[15:11];
  assign out_9 = in_1[15:0];

  // Other names for the same wires on the sheet: funct[5:0] = in_1[5:0]; IMM[15:0] = in_1[15:0]; Input[31:0] = in_1;
  //   label[25:0] = in_1[25:0]; s[4:0] = in_1[10:6]; rd[4:0] = in_1[15:11]; rt[4:0] = in_1[20:16];
  //   rs[4:0] = in_1[25:21]; op[5:0] = in_1[31:26]
endmodule

module Extender (
  input  [4:0] in_1,
  input  [15:0] in_2,
  output [31:0] out_3,
  output [31:0] out_4
);

  assign out_3 = {{27{in_1[4]}}, in_1};  // Bit_Extender bit_extender_1
  assign out_4 = {{16{in_2[15]}}, in_2};  // Bit_Extender bit_extender_2

  // Other names for the same wires on the sheet: eIMM[31:0] = out_4; es[31:0] = out_3; IMM[15:0] = in_2;
  //   s[4:0] = in_1
endmodule

module Syscall (
  input  in_1,
  input  in_2,
  output out_3
);

  wire not_1_out;

  not not_1 (not_1_out, in_1);
  or or_1 (out_3, not_1_out, in_2);

  // Other names for the same wires on the sheet: enable = out_3; eq = in_1; syscall = in_2
endmodule

module SumPeriod (
  input  in_1,
  input  in_2,
  input  in_3,
  output [15:0] out_4
);

  wire [15:0] adder_1_out, counter_1_q;

  Counter #(.width(16), .max('hffff)) counter_1 (
    .count(in_1), .Q(counter_1_q), .clk(in_2), .clr(in_3));  // open: load, D, carry
  Adder #(.width(16)) adder_1 (.a(16'h1), .b(counter_1_q), .out(adder_1_out));  // open: cin, cout
  Multiplexer #(.width(16), .disabled(0), .enable("false")) multiplexer_1 (
    .in0(adder_1_out), .in1(counter_1_q), .out(out_4), .sel(in_1));

  // Other names for the same wires on the sheet: CLK = in_2; cnt[15:0] = out_4; enable = in_1; RST = in_3
endmodule

module Syscall1 (
  input  in_1,
  input  in_2,
  input  in_3,
  input  [31:0] in_4,
  output [31:0] out_5
);

  Register #(.width(32)) register_1 (.D(in_4), .en(in_1), .Q(out_5), .clk(in_2), .clr(in_3));

  // Other names for the same wires on the sheet: CLK = in_2; enable = in_1; Input[31:0] = in_4; Output[31:0] = out_5;
  //   RST = in_3
endmodule

module IF_ID (
  input  [31:0] in_1,
  input  [31:0] in_2,
  input  \传输状态In ,
  input  CLK,
  input  \同步清零 ,
  output [31:0] out_6,
  output [31:0] out_7,
  output \传输状态Out 
);

  wire multiplexer_3_out;
  wire [31:0] multiplexer_1_out, multiplexer_2_out;

  Multiplexer #(.width(32), .enable("false")) multiplexer_1 (
    .in0(in_1), .in1({32{1'b0}}), .out(multiplexer_1_out), .sel(\同步清零 ));
  Multiplexer #(.width(32), .enable("false")) multiplexer_2 (
    .in0(in_2), .in1({32{1'b0}}), .out(multiplexer_2_out), .sel(\同步清零 ));
  Multiplexer #(.enable("false")) multiplexer_3 (.in0(\传输状态In ), .in1(1'b0), .out(multiplexer_3_out), .sel(\同步清零 ));
  Register #(.width(32)) register_1 (.D(multiplexer_1_out), .en(\传输状态In ), .Q(out_6), .clk(CLK));  // open: clr
  Register #(.width(32)) register_2 (.D(multiplexer_2_out), .en(\传输状态In ), .Q(out_7), .clk(CLK));  // open: clr
  Register #(.width(1)) register_3 (.D(multiplexer_3_out), .en(\传输状态In ), .Q(\传输状态Out ), .clk(CLK));  // open: clr
endmodule

module ID_EX (
  input  [4:0] in_1,
  input  [5:0] in_2,
  input  [5:0] in_3,
  input  [31:0] in_4,
  input  [31:0] in_5,
  input  [31:0] in_6,
  input  [31:0] in_7,
  input  \传输状态In ,
  input  CLK,
  input  \同步清零 ,
  output [4:0] out_11,
  output [5:0] out_12,
  output [5:0] out_13,
  output [31:0] out_14,
  output [31:0] out_15,
  output [31:0] out_16,
  output [31:0] out_17,
  output \传输状态Out 
);

  wire multiplexer_8_out;
  wire [4:0] multiplexer_1_out;
  wire [5:0] multiplexer_2_out, multiplexer_3_out;
  wire [31:0] multiplexer_4_out, multiplexer_5_out, multiplexer_6_out, multiplexer_7_out;

  Multiplexer #(.width(5), .enable("false")) multiplexer_1 (
    .in0(in_1), .in1({5{1'b0}}), .out(multiplexer_1_out), .sel(\同步清零 ));
  Multiplexer #(.width(6), .enable("false")) multiplexer_2 (
    .in0(in_2), .in1({6{1'b0}}), .out(multiplexer_2_out), .sel(\同步清零 ));
  Multiplexer #(.width(6), .enable("false")) multiplexer_3 (
    .in0(in_3), .in1({6{1'b0}}), .out(multiplexer_3_out), .sel(\同步清零 ));
  Multiplexer #(.width(32), .enable("false")) multiplexer_4 (
    .in0(in_4), .in1({32{1'b0}}), .out(multiplexer_4_out), .sel(\同步清零 ));
  Multiplexer #(.width(32), .enable("false")) multiplexer_5 (
    .in0(in_5), .in1({32{1'b0}}), .out(multiplexer_5_out), .sel(\同步清零 ));
  Multiplexer #(.width(32), .enable("false")) multiplexer_6 (
    .in0(in_6), .in1({32{1'b0}}), .out(multiplexer_6_out), .sel(\同步清零 ));
  Multiplexer #(.width(32), .enable("false")) multiplexer_7 (
    .in0(in_7), .in1({32{1'b0}}), .out(multiplexer_7_out), .sel(\同步清零 ));
  Multiplexer #(.enable("false")) multiplexer_8 (.in0(\传输状态In ), .in1(1'b0), .out(multiplexer_8_out), .sel(\同步清零 ));
  Register #(.width(5)) register_1 (.D(multiplexer_1_out), .en(\传输状态In ), .Q(out_11), .clk(CLK));  // open: clr
  Register #(.width(6)) register_2 (.D(multiplexer_2_out), .en(\传输状态In ), .Q(out_12), .clk(CLK));  // open: clr
  Register #(.width(6)) register_3 (.D(multiplexer_3_out), .en(\传输状态In ), .Q(out_13), .clk(CLK));  // open: clr
  Register #(.width(32)) register_4 (.D(multiplexer_4_out), .en(\传输状态In ), .Q(out_14), .clk(CLK));  // open: clr
  Register #(.width(32)) register_5 (.D(multiplexer_5_out), .en(\传输状态In ), .Q(out_15), .clk(CLK));  // open: clr
  Register #(.width(32)) register_6 (.D(multiplexer_6_out), .en(\传输状态In ), .Q(out_16), .clk(CLK));  // open: clr
  Register #(.width(32)) register_7 (.D(multiplexer_7_out), .en(\传输状态In ), .Q(out_17), .clk(CLK));  // open: clr
  Register #(.width(1)) register_8 (.D(multiplexer_8_out), .en(\传输状态In ), .Q(\传输状态Out ), .clk(CLK));  // open: clr
endmodule

module EX_MEM (
  input  [4:0] in_1,
  input  [5:0] in_2,
  input  [31:0] in_3,
  input  [31:0] in_4,
  input  \传输状态In ,
  input  CLK,
  input  \同步清零 ,
  output [4:0] out_8,
  output [5:0] out_9,
  output [31:0] out_10,
  output [31:0] out_11,
  output \传输状态Out 
);

  wire multiplexer_5_out;
  wire [4:0] multiplexer_1_out;
  wire [5:0] multiplexer_2_out;
  wire [31:0] multiplexer_3_out, multiplexer_4_out;

  Multiplexer #(.width(5), .enable("false")) multiplexer_1 (
    .in0(in_1), .in1({5{1'b0}}), .out(multiplexer_1_out), .sel(\同步清零 ));
  Multiplexer #(.width(6), .enable("false")) multiplexer_2 (
    .in0(in_2), .in1({6{1'b0}}), .out(multiplexer_2_out), .sel(\同步清零 ));
  Multiplexer #(.width(32), .enable("false")) multiplexer_3 (
    .in0(in_3), .in1({32{1'b0}}), .out(multiplexer_3_out), .sel(\同步清零 ));
  Multiplexer #(.width(32), .enable("false")) multiplexer_4 (
    .in0(in_4), .in1({32{1'b0}}), .out(multiplexer_4_out), .sel(\同步清零 ));
  Multiplexer #(.enable("false")) multiplexer_5 (.in0(\传输状态In ), .in1(1'b0), .out(multiplexer_5_out), .sel(\同步清零 ));
  Register #(.width(5)) register_1 (.D(multiplexer_1_out), .en(\传输状态In ), .Q(out_8), .clk(CLK));  // open: clr
  Register #(.width(6)) register_2 (.D(multiplexer_2_out), .en(\传输状态In ), .Q(out_9), .clk(CLK));  // open: clr
  Register #(.width(32)) register_3 (.D(multiplexer_3_out), .en(\传输状态In ), .Q(out_10), .clk(CLK));  // open: clr
  Register #(.width(32)) register_4 (.D(multiplexer_4_out), .en(\传输状态In ), .Q(out_11), .clk(CLK));  // open: clr
  Register #(.width(1)) register_5 (.D(multiplexer_5_out), .en(\传输状态In ), .Q(\传输状态Out ), .clk(CLK));  // open: clr
endmodule

module MEM_WB (
  input  [4:0] in_1,
  input  [31:0] in_2,
  input  [31:0] in_3,
  input  \传输状态In ,
  input  CLK,
  input  \同步清零 ,
  output [4:0] out_7,
  output [31:0] out_8,
  output [31:0] out_9,
  output \传输状态Out 
);

  wire multiplexer_4_out;
  wire [4:0] multiplexer_1_out;
  wire [31:0] multiplexer_2_out, multiplexer_3_out;

  Multiplexer #(.width(5), .enable("false")) multiplexer_1 (
    .in0(in_1), .in1({5{1'b0}}), .out(multiplexer_1_out), .sel(\同步清零 ));
  Multiplexer #(.width(32), .enable("false")) multiplexer_2 (
    .in0(in_2), .in1({32{1'b0}}), .out(multiplexer_2_out), .sel(\同步清零 ));
  Multiplexer #(.width(32), .enable("false")) multiplexer_3 (
    .in0(in_3), .in1({32{1'b0}}), .out(multiplexer_3_out), .sel(\同步清零 ));
  Multiplexer #(.enable("false")) multiplexer_4 (.in0(\传输状态In ), .in1(1'b0), .out(multiplexer_4_out), .sel(\同步清零 ));
  Register #(.width(5)) register_1 (.D(multiplexer_1_out), .en(\传输状态In ), .Q(out_7), .clk(CLK));  // open: clr
  Register #(.width(32)) register_2 (.D(multiplexer_2_out), .en(\传输状态In ), .Q(out_8), .clk(CLK));  // open: clr
  Register #(.width(32)) register_3 (.D(multiplexer_3_out), .en(\传输状态In ), .Q(out_9), .clk(CLK));  // open: clr
  Register #(.width(1)) register_4 (.D(multiplexer_4_out), .en(\传输状态In ), .Q(\传输状态Out ), .clk(CLK));  // open: clr
endmodule
